# Fritzing sketch lightgate-sketch (saved by Fritzing 0.9.5d)
breadboards: 1

parts:
  Part1 = Arduino Uno (Rev3)
  R2 = PHOTOCELL [package=photocell]
  U1 = LCD-16X2 [package=lcd-16x2]
  U2 = POT [package=3362u]
  R3 = Resistor [tolerance=±5% resistance=10k package="1206 [SMD]"]

nets:
  N1: Part1.A0, R2.P$1, R3.Pin_0
  N2: Part1.D11_PWM/MOSI, U1.E
  N3: Part1.D12/MISO, U1.RS
  N4: Part1.D2, U1.DB7
  N5: Part1.D3_PWM, U1.DB6
  N6: Part1.D4, U1.DB5
  N7: Part1.D5_PWM, U1.DB4
  5V: Part1.5V, R2.P$2, U1.VDD, U1.A, U2.A
  GND: Part1.GND, U1.VSS, U1.R_W, U1.K, U2.E, R3.Pin_1
  N8: U1.VO, U2.S
